# Fritzing sketch DisplayBank (saved by Fritzing 0.9.0b)
circuit board: 5cm x 5.6cm
breadboards: 1

parts:
  U1 = 74HC595 [package="DIP16 [THT]"]
  U2 = 74HC595 [package="DIP16 [THT]"]
  U3 = attiny85 [package=dip]
  R1 = Resistor [tolerance=±5% resistance=220 package=THT]
  R2 = Resistor [tolerance=±5% resistance=220 package=THT]
  R3 = Resistor [tolerance=±5% resistance=220 package=THT]
  R4 = Resistor [tolerance=±5% resistance=220 package=THT]
  JP1 = Header 4 [package=screwterminal-3.5mm-4_lock]
  R5 = Resistor [tolerance=±5% resistance=10k package=THT]
  U4 = 7-SEGMENT-4DIGIT [package=7-segment-4digit]  # not connected
  U4_2 = 7-SEGMENT-4DIGIT [package=7-segment-4digit]  # not connected
  U4_3 = 7-SEGMENT-4DIGIT [package=7-segment-4digit]  # not connected

nets:
  GND: U1.GND, U1.OE, U2.GND, U2.OE, U3.Pin_4, JP1.4
  N1: U1.Q7', U2.DS
  VCC: U1.MR, U1.VCC, U2.MR, U2.VCC, U3.Pin_8
  N2: U1.SH_CP, U2.SH_CP, U3.Pin_5
  N3: U1.ST_CP, U2.ST_CP, U3.Pin_6
  N4: U1.DS, U3.Pin_7
  N5: U2.Q1, R4.Pin_1
  N6: U2.Q2, R3.Pin_1
  N7: U2.Q3, R2.Pin_1
  N8: U2.Q4, R1.Pin_1
  N9: U3.Pin_1, R5.Pin_1
  N10: U3.Pin_2, JP1.2
  N11: U3.Pin_3, JP1.3
  N12: JP1.1, R5.Pin_0
