# Fritzing sketch Book Project (saved by Fritzing 0.9.3b)
circuit board: 7.45434cm x 3.60032cm
breadboards: 1

parts:
  U1 = atmega328 [package=dip]
  U2 = microSD Socket [package=micro-sd-socket-pp]
  R1 = Resistor [tolerance=±5% resistance=10k package=THT]
  Pg_1 = molex pin header, 2 pins [form=molex]
  Power = molex pin header, 2 pins [form=molex]
  part = Resistor [tolerance=±5% resistance=10k package=THT]
  Pg_2 = molex pin header, 2 pins [form=molex]
  Pg_3 = molex pin header, 2 pins [form=molex]
  Pg_4 = molex pin header, 2 pins [form=molex]
  Pg_5 = molex pin header, 2 pins [form=molex]
  Pg_6 = molex pin header, 2 pins [form=molex]
  Pg_7 = molex pin header, 2 pins [form=molex]
  Pg_8 = molex pin header, 2 pins [form=molex]
  R2 = Resistor [tolerance=±5% resistance=10k package=THT]
  R3 = Resistor [tolerance=±5% resistance=10k package=THT]
  R4 = Resistor [tolerance=±5% resistance=10k package=THT]
  R5 = Resistor [tolerance=±5% resistance=10k package=THT]
  R6 = Resistor [tolerance=±5% resistance=10k package=THT]
  R7 = Resistor [tolerance=±5% resistance=10k package=THT]
  R8 = Resistor [tolerance=±5% resistance=10k package=THT]
  Spkr = molex pin header, 2 pins [form=molex]
  Micro_SD = Header 6 [package=molex-1x6-ra]

nets (from the pcb view):
  N1: U1.RESET, part.Pin_1
  N2: U1.D0_(RX), Pg_1.pin2
  N3: U1.D1_(TX), Pg_2.pin2
  N4: U1.D2, Pg_3.pin2
  N5: U1.D3_(PWM), Pg_4.pin2
  VCC: U1.VCC, U2.VCC, Power.pin1, part.Pin_0, Micro_SD.6
  N6: U1.D5_(PWM), Pg_5.pin2
  N7: U1.D6_(PWM), Pg_6.pin2
  N8: U1.D7, Pg_7.pin2
  N9: U1.D8, Pg_8.pin2
  N10: U1.D9_(PWM), Spkr.pin1
  N11: U1.D10_(PWM), U2.CS, Micro_SD.1
  N12: U1.D11_(PWM), U2.DI, Micro_SD.2
  N13: U1.D13, U2.SCK, Micro_SD.3, Micro_SD.4
  N14: U2.GND, R1.Pin_0, Power.pin2, R2.Pin_0, R3.Pin_0, R4.Pin_0, R5.Pin_0, R6.Pin_0, R7.Pin_0, R8.Pin_0, Spkr.pin2, Micro_SD.5
  N15: R1.Pin_1, Pg_1.pin1
  N16: Pg_2.pin1, R2.Pin_1
  N17: Pg_3.pin1, R3.Pin_1
  N18: Pg_4.pin1, R4.Pin_1
  N19: Pg_5.pin1, R5.Pin_1
  N20: Pg_6.pin1, R6.Pin_1
  N21: Pg_7.pin1, R7.Pin_1
  N22: Pg_8.pin1, R8.Pin_1
