# Fritzing sketch NaniteSMD (saved by Fritzing 0.9.2b)
circuit board: 8.46667cm x 5.64444cm
breadboards: 1

parts:
  3_6v = DIODE-ZENER [package=diode-zener]
  3_6v_2 = DIODE-ZENER [package=diode-zener]
  USB_MiniB = USB Connectors [package=usb-minib-nostop]
  ATTiny85 = ATTINY13 [package=so]
  S2 = Momentary Switch [package=tactile_switch_smd]
  U1 = attiny85 [package=dip]
  LED1 = smd LED [color="Red (633nm)" package="0805 [SMD]"]
  68 = Resistor [tolerance=±0.05% resistance=2.2k package="0805 [SMD]"]
  68_2 = Resistor [tolerance=±0.05% resistance=68 package="0805 [SMD]"]
  R2 = Resistor [tolerance=±5% resistance=220 package="0805 [SMD]"]
  R1 = Resistor [tolerance=±5% resistance=10k package="0805 [SMD]"]

nets:
  N1: 3_6v.C, USB_MiniB.D-, 68_2.Pin_0
  GND: 3_6v.A, 3_6v_2.A, USB_MiniB.GND, ATTiny85.GND, S2.3, U1.Pin_4
  N2: 3_6v_2.C, USB_MiniB.D+, 68.Pin_0
  5V: USB_MiniB.VBUS, ATTiny85.VCC, U1.Pin_8, R2.Pin_0, R1.Pin_1
  N3: ATTiny85.PB5(NRES), S2.1, U1.Pin_1, LED1.cathode
  N4: ATTiny85.PB3(ADC3), U1.Pin_3, 68_2.Pin_1
  N5: ATTiny85.PB4(ADC2), U1.Pin_2, 68.Pin_1
  N6: ATTiny85.PB0(MOSI), U1.Pin_5
  N7: ATTiny85.PB1(MISO), U1.Pin_6
  N8: ATTiny85.PB2(SCK_ADC1), U1.Pin_7
  N9: LED1.anode, R2.Pin_1
